# Fritzing sketch fritzing-general (saved by Fritzing 0.9.3b)

parts:
  Componente1 = Arduino Uno (Rev3) - ICSP
  LED1 = LEDs [package=led10mm]  # not connected
  R1 = Resistor [tolerance=±5% resistance=220 package=THT]
  LED2 = LEDs [package=led10mm]  # not connected
  R2 = Resistor [tolerance=±5% resistance=220 package=THT]
  LED3 = LEDs [package=led10mm]  # not connected
  R3 = Resistor [tolerance=±5% resistance=220 package=THT]
  LED4 = LEDs [package=led10mm]  # not connected
  R4 = Resistor [tolerance=±5% resistance=220 package=THT]
  R5 = Resistor [tolerance=±5% resistance=220 package=THT]  # not connected
  LED5 = LEDs [package=led10mm]

nets:
  N1: Componente1.D1/TX, R4.Pin_0
  N2: Componente1.D2, R3.Pin_0
  N3: Componente1.D3_PWM, R2.Pin_0
  N4: Componente1.D4, R1.Pin_0
  N5: Componente1.GND, LED5.A
